# Fritzing sketch Esp32-ADXL345 Sparkfun (saved by Fritzing 0.9.9b)

parts:
  U1 = ESP32S-HiLetgo [part_number="ESP32 DevKit C"]
  A1 = Triple Axis Accelerometer Breakout - ADXL345

nets:
  N1: U1.3.3, A1.VCC, A1.CS
  N2: U1.GND, A1.SDO
  N3: U1.GPIO21, A1.SDA
  N4: U1.GPIO22, A1.SCL

notes:
  //////////////////////////////////////////////////////////////////////
  // When connecting to an ESP32 device,
  // configure the I2C GPIOs used for the bus
  //////////////////////////////////////////////////////////////////////
  Configuration.SetPinFunction(21, DeviceFunction.I2C1_DATA);
  Configuration.SetPinFunction(22, DeviceFunction.I2C1_CLOCK);

custom parts:
  ESP32S-HiLetgo: HiLetgo ESP-WROOM-32 ESP32 ESP-32S Development Board 2.4GHz Dual-Mode WiFi + Bluetooth Dual Cores Microcontroller The ESP32 integrated with Antenna switches, RF Balun, power amplifiers, low-noise amplifiers, filters, and management modules, and the entire solution occupies the least area of PCB. 2.4 GHz Wi-Fi plus Bluetooth dual-mode chip, with TSMC Ultra-low power consumption 40nm technology,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
